// Logisim project Lab04_ALU.circ as structural Verilog: 7 circuits, main circuit main
module main (
  input  CIn,
  input  [3:0] InA,
  input  [3:0] InB,
  input  [2:0] Sel,
  input  Mode,
  output COut,
  output Cmp,
  output [3:0] ALUOut
);

  ALU alu_1 (.CIn(CIn), .InA(InA), .InB(InB), .Sel(Sel), .Mode(Mode), .COut(COut), .Cmp(Cmp), .ALUOut(ALUOut));

  // Notes on the sheet:
  //   Name
  //   Lab 04: ALU
  //   Date
  //   Arithmetic Codes
  //   0=-1
  //   1=A-1
  //   2=A+B
  //   3=A-B
  //   4=AB-1
  //   5=AB'-1
  //   6=A+A
  //   7=A+1
  //   Mode: H=Logic, L=Arithmetic
  //   Logic Codes
  //   0=AB
  //   1=(AB)'
  //   2=A+B
  //   3=(A+B)'
  //   4=A Xor B
  //   5=AB'
  //   6=A+B'
  //   7=A'
endmodule

module ALU (
  input  CIn,
  input  [3:0] InA,
  input  [3:0] InB,
  input  [2:0] Sel,
  input  Mode,
  output COut,
  output Cmp,
  output [3:0] ALUOut
);

  wire [3:0] arithmetic_1_arout, logic_1_loout;

  Arithmetic arithmetic_1 (
    .CIn(CIn), .InA(InA), .InB(InB), .Sel(Sel), .ArOut(arithmetic_1_arout), .COut(COut), .Cmp(Cmp));
  Multiplexer #(.width(4)) multiplexer_1 (.in0(arithmetic_1_arout), .in1(logic_1_loout), .out(ALUOut), .sel(Mode));
  Logic logic_1 (.InA(InA), .InB(InB), .Sel(Sel), .LoOut(logic_1_loout));

  // Notes on the sheet:
  //   Mode: H=Logic, L=Aritmetic
  //   Arithmetic Codes
  //   0=-1
  //   1=A-1
  //   2=A+B
  //   3=A-B
  //   4=AB-1
  //   5=AB'-1
  //   6=A+A
  //   7=A+1
  //   Mode: H=Logic, L=Aritmetic
  //   Logic Codes
  //   0=AB
  //   1=(AB)'
  //   2=A+B
  //   3=(A+B)'
  //   4=A Xor B
  //   5=AB'
  //   6=A+B'
  //   7=A'
endmodule

module Arithmetic (
  input  CIn,
  input  [3:0] InA,
  input  [3:0] InB,
  input  [2:0] Sel,
  output [3:0] ArOut,
  output COut,
  output Cmp
);

  wire adder_1_cout, adder_2_cout, adder_3_cout, subtractor_1_bout, subtractor_2_bout, subtractor_3_bout,
       subtractor_4_bout;
  wire [3:0] adder_1_out, adder_2_out, adder_3_out, multiplier_1_out, multiplier_2_out, not_1_out,
       subtractor_1_out, subtractor_2_out, subtractor_3_out, subtractor_4_out;

  Adder #(.width(4)) adder_1 (.a(InA), .b(InB), .out(adder_1_out), .cin(CIn), .cout(adder_1_cout));
  Subtractor #(.width(4)) subtractor_1 (.a(InA), .b(InB), .out(subtractor_1_out), .bin(CIn), .bout(subtractor_1_bout));
  Multiplier #(.width(4)) multiplier_1 (.a(InA), .b(InB), .out(multiplier_1_out));  // open: cin, cout
  Multiplier #(.width(4)) multiplier_2 (.a(InA), .b(not_1_out), .out(multiplier_2_out));  // open: cin, cout
  assign not_1_out = ~InB;  // NOT_Gate not_1, 4 bits wide
  Adder #(.width(4)) adder_2 (.a(InA), .b(InA), .out(adder_2_out), .cin(CIn), .cout(adder_2_cout));
  Adder #(.width(4)) adder_3 (.a(InA), .b(4'b0001), .out(adder_3_out), .cin(CIn), .cout(adder_3_cout));
  Comparator #(.mode("unsigned"), .width(4)) comparator_1 (.a(InA), .b(InB), .eq(Cmp));  // open: gt, lt
  Subtractor #(.width(4)) subtractor_2 (
    .a(InA), .b(4'b0001), .out(subtractor_2_out), .bin(CIn), .bout(subtractor_2_bout));
  Subtractor #(.width(4)) subtractor_3 (
    .a(multiplier_1_out), .b(4'b0001), .out(subtractor_3_out), .bout(subtractor_3_bout));  // open: bin
  Subtractor #(.width(4)) subtractor_4 (
    .a(multiplier_2_out), .b(4'b0001), .out(subtractor_4_out), .bout(subtractor_4_bout));  // open: bin
  Multiplexer #(.select(3), .width(4)) multiplexer_1 (
    .in0(4'b1111), .in1(subtractor_2_out), .in2(adder_1_out), .in3(subtractor_1_out), .in4(subtractor_3_out),
    .in5(subtractor_4_out), .in6(adder_2_out), .in7(adder_3_out), .out(ArOut), .sel(Sel));
  Multiplexer #(.select(3)) multiplexer_2 (
    .in0(1'b0), .in1(subtractor_2_bout), .in2(adder_1_cout), .in3(subtractor_1_bout),
    .in4(subtractor_3_bout), .in5(subtractor_4_bout), .in6(adder_2_cout), .in7(adder_3_cout), .out(COut),
    .sel(Sel));

  // Notes on the sheet:
  //   0=-1
  //   1=A-1
  //   2=A+B
  //   3=A-B
  //   4=AB-1
  //   5=AB'-1
  //   6=A+A
  //   7=A+1
  //   Arithmetic Subcircuit
endmodule

module Logic (
  input  [3:0] InA,
  input  [3:0] InB,
  input  [2:0] Sel,
  output [3:0] LoOut
);

  wire [3:0] logicand4bits_1_logicand, logicand4bits_2_logicand, logicand4bits_3_logicand,
       logicor4bits_1_logicor, logicor4bits_2_logicor, logicor4bits_3_logicor, logicxor4bits_1_logicxor,
       not_1_out, not_2_out, not_3_out, not_4_out, not_5_out;

  assign not_1_out = ~InB;  // NOT_Gate not_1, 4 bits wide
  assign not_2_out = ~InB;  // NOT_Gate not_2, 4 bits wide
  LogicAnd4bits logicand4bits_1 (.InA(InA), .InB(InB), .LogicAnd(logicand4bits_1_logicand));
  LogicAnd4bits logicand4bits_2 (.InA(InA), .InB(InB), .LogicAnd(logicand4bits_2_logicand));
  LogicOr4bits logicor4bits_1 (.InA(InA), .InB(InB), .LogicOr(logicor4bits_1_logicor));
  assign not_3_out = ~logicor4bits_2_logicor;  // NOT_Gate not_3, 4 bits wide
  LogicOr4bits logicor4bits_2 (.InA(InA), .InB(InB), .LogicOr(logicor4bits_2_logicor));
  LogicXor4bits logicxor4bits_1 (.InA(InA), .InB(InB), .LogicXor(logicxor4bits_1_logicxor));
  LogicAnd4bits logicand4bits_3 (.InA(InA), .InB(not_1_out), .LogicAnd(logicand4bits_3_logicand));
  LogicOr4bits logicor4bits_3 (.InA(InA), .InB(not_2_out), .LogicOr(logicor4bits_3_logicor));
  assign not_4_out = ~logicand4bits_2_logicand;  // NOT_Gate not_4, 4 bits wide
  assign not_5_out = ~InA;  // NOT_Gate not_5, 4 bits wide
  Multiplexer #(.select(3), .width(4)) multiplexer_1 (
    .in0(logicand4bits_1_logicand), .in1(not_4_out), .in2(logicor4bits_1_logicor), .in3(not_3_out),
    .in4(logicxor4bits_1_logicxor), .in5(logicand4bits_3_logicand), .in6(logicor4bits_3_logicor),
    .in7(not_5_out), .out(LoOut), .sel(Sel));

  // Notes on the sheet:
  //   0=AB
  //   5=AB'
  //   7=A'
  //   Logic Subcircuit
  //   1=(AB)'
  //   2=A+B
  //   3=(A+B)'
  //   4=A Xor B
  //   6=A+B'
endmodule

module LogicAnd4bits (
  input  [3:0] InA,
  input  [3:0] InB,
  output [3:0] LogicAnd
);

  and and_1 (LogicAnd[0], InA[0], InB[0]);
  and and_2 (LogicAnd[1], InA[1], InB[1]);
  and and_3 (LogicAnd[2], InA[2], InB[2]);
  and and_4 (LogicAnd[3], InA[3], InB[3]);
endmodule

module LogicOr4bits (
  input  [3:0] InA,
  input  [3:0] InB,
  output [3:0] LogicOr
);

  or or_1 (LogicOr[0], InA[0], InB[0]);
  or or_2 (LogicOr[1], InA[1], InB[1]);
  or or_3 (LogicOr[2], InA[2], InB[2]);
  or or_4 (LogicOr[3], InA[3], InB[3]);
endmodule

module LogicXor4bits (
  input  [3:0] InA,
  input  [3:0] InB,
  output [3:0] LogicXor
);

  xor xor_1 (LogicXor[0], InA[0], InB[0]);
  xor xor_2 (LogicXor[1], InA[1], InB[1]);
  xor xor_3 (LogicXor[2], InA[2], InB[2]);
  xor xor_4 (LogicXor[3], InA[3], InB[3]);
endmodule
