// Logisim project Lab5_FlipFlop_Counters.circ as structural Verilog: 7 circuits, main circuit main
module main (
  input  Reset,
  input  [2:0] Sel,
  output [3:0] Cnt
);

  wire Clk_out;

  Clock #(.highDuration(4), .lowDuration(4)) Clk (.out(Clk_out));
  Clock sysclk ();  // open: out
  Universal universal_counter (.Clk(Clk_out), .Reset(Reset), .SelectCounter(Sel), .Cnt(Cnt));
  Hex_Digit_Display hex_digit_display_1 (.value(Cnt));  // open: dp
endmodule

module AsyncUpCnt (
  input  Clk,
  input  Rst,
  output [3:0] Up
);

  wire d_ff_1_qn, d_ff_2_qn, d_ff_3_qn, d_ff_4_qn;

  D_Flip_Flop d_ff_1 (.D(d_ff_1_qn), .clk(Clk), .Q(Up[0]), .Qn(d_ff_1_qn), .reset(Rst));  // open: preset
  D_Flip_Flop d_ff_2 (.D(d_ff_2_qn), .clk(d_ff_1_qn), .Q(Up[1]), .Qn(d_ff_2_qn), .reset(Rst));  // open: preset
  D_Flip_Flop d_ff_3 (.D(d_ff_3_qn), .clk(d_ff_2_qn), .Q(Up[2]), .Qn(d_ff_3_qn), .reset(Rst));  // open: preset
  D_Flip_Flop d_ff_4 (.D(d_ff_4_qn), .clk(d_ff_3_qn), .Q(Up[3]), .Qn(d_ff_4_qn), .reset(Rst));  // open: preset
endmodule

module AsyncDownCnt (
  input  Clk,
  input  Reset,
  output [3:0] Down
);

  wire d_ff_1_qn, d_ff_2_qn, d_ff_3_qn, d_ff_4_qn;

  D_Flip_Flop d_ff_1 (.D(d_ff_1_qn), .clk(Clk), .Q(Down[0]), .Qn(d_ff_1_qn), .preset(Reset));  // open: reset
  D_Flip_Flop d_ff_2 (.D(d_ff_2_qn), .clk(Down[0]), .Q(Down[1]), .Qn(d_ff_2_qn), .preset(Reset));  // open: reset
  D_Flip_Flop d_ff_3 (.D(d_ff_3_qn), .clk(Down[1]), .Q(Down[2]), .Qn(d_ff_3_qn), .preset(Reset));  // open: reset
  D_Flip_Flop d_ff_4 (.D(d_ff_4_qn), .clk(Down[2]), .Q(Down[3]), .Qn(d_ff_4_qn), .preset(Reset));  // open: reset
endmodule

module AsyncDecCnt (
  input  Clk,
  input  Reset,
  output [3:0] Decade
);

  wire and_1_out, d_ff_1_qn, d_ff_2_qn, d_ff_3_qn, d_ff_4_qn, or_1_out;

  D_Flip_Flop d_ff_1 (.D(d_ff_1_qn), .clk(Clk), .Q(Decade[0]), .Qn(d_ff_1_qn), .reset(or_1_out));  // open: preset
  or or_1 (or_1_out, Reset, and_1_out);
  D_Flip_Flop d_ff_2 (.D(d_ff_2_qn), .clk(d_ff_1_qn), .Q(Decade[1]), .Qn(d_ff_2_qn), .reset(or_1_out));  // open: preset
  D_Flip_Flop d_ff_3 (.D(d_ff_3_qn), .clk(d_ff_2_qn), .Q(Decade[2]), .Qn(d_ff_3_qn), .reset(or_1_out));  // open: preset
  D_Flip_Flop d_ff_4 (.D(d_ff_4_qn), .clk(d_ff_3_qn), .Q(Decade[3]), .Qn(d_ff_4_qn), .reset(or_1_out));  // open: preset
  and and_1 (and_1_out, Decade[3], Decade[1]);
endmodule

module SyncRingCnt (
  input  Clk,
  input  Reset,
  output [3:0] Ring
);

  D_Flip_Flop d_ff_1 (.D(Ring[3]), .clk(Clk), .Q(Ring[0]), .preset(Reset));  // open: Qn, reset
  D_Flip_Flop d_ff_2 (.D(Ring[0]), .clk(Clk), .Q(Ring[1]), .reset(Reset));  // open: Qn, preset
  D_Flip_Flop d_ff_3 (.D(Ring[1]), .clk(Clk), .Q(Ring[2]), .reset(Reset));  // open: Qn, preset
  D_Flip_Flop d_ff_4 (.D(Ring[2]), .clk(Clk), .Q(Ring[3]), .reset(Reset));  // open: Qn, preset
endmodule

module SyncJohnsonCnt (
  input  Clk,
  input  Reset,
  output [3:0] Johnson
);

  wire d_ff_4_qn;

  D_Flip_Flop d_ff_1 (.D(d_ff_4_qn), .clk(Clk), .Q(Johnson[0]), .preset(Reset));  // open: Qn, reset
  D_Flip_Flop d_ff_2 (.D(Johnson[0]), .clk(Clk), .Q(Johnson[1]), .reset(Reset));  // open: Qn, preset
  D_Flip_Flop d_ff_3 (.D(Johnson[1]), .clk(Clk), .Q(Johnson[2]), .reset(Reset));  // open: Qn, preset
  D_Flip_Flop d_ff_4 (.D(Johnson[2]), .clk(Clk), .Q(Johnson[3]), .Qn(d_ff_4_qn), .reset(Reset));  // open: preset
endmodule

module Universal (
  input  Clk,
  input  Reset,
  input  [2:0] SelectCounter,
  output [3:0] Cnt
);

  wire [3:0] decimal_counter_decade, down_counter_down, Johnson_counter_johnson, ring_counter_ring,
       up_counter_up;

  AsyncUpCnt up_counter (.Clk(Clk), .Rst(Reset), .Up(up_counter_up));
  AsyncDownCnt down_counter (.Clk(Clk), .Reset(Reset), .Down(down_counter_down));
  AsyncDecCnt decimal_counter (.Clk(Clk), .Reset(Reset), .Decade(decimal_counter_decade));
  SyncRingCnt ring_counter (.Clk(Clk), .Reset(Reset), .Ring(ring_counter_ring));
  SyncJohnsonCnt Johnson_counter (.Clk(Clk), .Reset(Reset), .Johnson(Johnson_counter_johnson));
  Multiplexer #(.select(3), .width(4)) multiplexer_1 (
    .in0(up_counter_up), .in1(down_counter_down), .in2(decimal_counter_decade), .in3(ring_counter_ring),
    .in4(Johnson_counter_johnson), .in5(4'b0000), .in6(4'b0000), .in7(4'b0000), .out(Cnt), .sel(SelectCounter));
endmodule
